// Logisim project my_lc4_logisim_circuit.circ as structural Verilog
module mux_two_in_out (
  input  [15:0] Input1,
  input  [15:0] Input2,
  input  [15:0] Input3,
  input  [15:0] Input4,
  input  [15:0] Input5,
  input  [15:0] Input6,
  input  [15:0] Input7,
  input  [15:0] Input8,
  input  [2:0] Select1,
  input  [2:0] Select2,
  output [15:0] Output1,
  output [15:0] Output2
);

  Multiplexer #(.select(3), .width(16)) multiplexer_1 (
    .in0(Input1), .in1(Input2), .in2(Input3), .in3(Input4), .in4(Input5), .in5(Input6), .in6(Input7),
    .in7(Input8), .out(Output1), .sel(Select1));
  Multiplexer #(.select(3), .width(16)) multiplexer_2 (
    .in0(Input1), .in1(Input2), .in2(Input3), .in3(Input4), .in4(Input5), .in5(Input6), .in6(Input7),
    .in7(Input8), .out(Output2), .sel(Select2));

  // Notes on the sheet:
  //   A MUX variation which has two select lines and two output lines.
endmodule

module decoder_variant (
  input  WE,
  input  [2:0] in_2,
  output Output1,
  output Output2,
  output Output3,
  output Output4,
  output Output5,
  output Output6,
  output Output7,
  output Output8
);

  wire not_1_out, not_2_out, not_3_out, not_4_out, not_5_out, not_6_out, not_7_out, not_8_out, not_9_out,
       not_10_out, not_11_out, not_12_out;

  not not_1 (not_1_out, in_2[0]);
  not not_2 (not_2_out, in_2[1]);
  not not_3 (not_3_out, in_2[2]);
  not not_4 (not_4_out, in_2[1]);
  not not_5 (not_5_out, in_2[2]);
  not not_6 (not_6_out, in_2[0]);
  not not_7 (not_7_out, in_2[2]);
  not not_8 (not_8_out, in_2[2]);
  not not_9 (not_9_out, in_2[0]);
  not not_10 (not_10_out, in_2[1]);
  not not_11 (not_11_out, in_2[1]);
  not not_12 (not_12_out, in_2[0]);
  and and_1 (Output1, WE, not_1_out, not_2_out, not_3_out);
  and and_2 (Output2, WE, in_2[0], not_4_out, not_5_out);
  and and_3 (Output3, WE, not_6_out, in_2[1], not_7_out);
  and and_4 (Output4, WE, not_8_out, in_2[1], in_2[0]);
  and and_5 (Output5, WE, not_9_out, not_10_out, in_2[2]);
  and and_6 (Output6, WE, in_2[2], not_11_out, in_2[0]);
  and and_7 (Output7, WE, not_12_out, in_2[2], in_2[1]);
  and and_8 (Output8, WE, in_2[2], in_2[1], in_2[0]);

  // Notes on the sheet:
  //   Decoder with a "Write Enable". When WE=0, the output is always 0
endmodule

module simple_memory_register (
  input  Clock,
  input  WE,
  input  [2:0] AddressWrite,
  input  [15:0] DataIn,
  input  [2:0] AddressRead1,
  input  [2:0] AddressRead2,
  output [15:0] DataOut1,
  output [15:0] DataOut2
);

  wire decoder_1_out0, decoder_1_out1, decoder_1_out2, decoder_1_out3, decoder_1_out4, decoder_1_out5,
       decoder_1_out6, decoder_1_out7;
  wire [15:0] register_1_q, register_2_q, register_3_q, register_4_q, register_5_q, register_6_q,
       register_7_q, register_8_q;

  Decoder #(.select(3)) decoder_1 (
    .out0(decoder_1_out0), .out1(decoder_1_out1), .out2(decoder_1_out2), .out3(decoder_1_out3),
    .out4(decoder_1_out4), .out5(decoder_1_out5), .out6(decoder_1_out6), .out7(decoder_1_out7),
    .sel(AddressWrite), .en(WE));
  Register #(.width(16)) register_1 (.D(DataIn), .en(decoder_1_out0), .clk(Clock), .Q(register_1_q));  // open: clr
  Register #(.width(16)) register_2 (.D(DataIn), .en(decoder_1_out1), .clk(Clock), .Q(register_2_q));  // open: clr
  Register #(.width(16)) register_3 (.D(DataIn), .en(decoder_1_out2), .clk(Clock), .Q(register_3_q));  // open: clr
  Register #(.width(16)) register_4 (.D(DataIn), .en(decoder_1_out3), .clk(Clock), .Q(register_4_q));  // open: clr
  Register #(.width(16)) register_5 (.D(DataIn), .en(decoder_1_out4), .clk(Clock), .Q(register_5_q));  // open: clr
  Register #(.width(16)) register_6 (.D(DataIn), .en(decoder_1_out5), .clk(Clock), .Q(register_6_q));  // open: clr
  Register #(.width(16)) register_7 (.D(DataIn), .en(decoder_1_out6), .clk(Clock), .Q(register_7_q));  // open: clr
  Register #(.width(16)) register_8 (.D(DataIn), .en(decoder_1_out7), .clk(Clock), .Q(register_8_q));  // open: clr
  mux_two_in_out mux_two_in_out_1 (
    .Input1(register_1_q), .Input2(register_2_q), .Input3(register_3_q), .Input4(register_4_q),
    .Input5(register_5_q), .Input6(register_6_q), .Input7(register_7_q), .Input8(register_8_q),
    .Select1(AddressRead1), .Select2(AddressRead2), .Output1(DataOut1), .Output2(DataOut2));

  // Notes on the sheet:
  //   8 by 16 Register File
endmodule

module lc4_alu_splitter (
  input  [15:0] Instruction,
  output [5:0] I_5_0,
  output [6:0] I_6_0,
  output [4:0] I_4_0,
  output [7:0] I_7_0,
  output [8:0] I_8_0,
  output [3:0] I_3_0
);


  assign I_3_0 = Instruction[3:0];
  assign I_4_0 = Instruction[4:0];
  assign I_5_0 = Instruction[5:0];
  assign I_6_0 = Instruction[6:0];
  assign I_7_0 = Instruction[7:0];
  assign I_8_0 = Instruction[8:0];
endmodule

module lc4_alu_comparator (
  input  [1:0] ControlSignal,
  input  [15:0] Rs,
  input  [15:0] Rt,
  input  [15:0] Instruction,
  output [15:0] SignOutput
);

  wire [1:0] multiplexer_2_out;
  wire [2:0] comparator_1_gt, comparator_2_gt, multiplexer_1_out;

  Bit_Extender bit_extender_1 (.in(Instruction[7:0]));  // open: out
  Bit_Extender #(.\type ("zero")) bit_extender_2 (.in(Instruction[7:0]));  // open: out
  Comparator #(.width(16)) comparator_1 (
    .a(Rs), .b(Rt), .gt(comparator_1_gt[0]), .eq(comparator_1_gt[1]), .lt(comparator_1_gt[2]));
  Comparator #(.mode("unsigned"), .width(16)) comparator_2 (
    .a(Rs), .b(Rt), .gt(comparator_2_gt[0]), .eq(comparator_2_gt[1]), .lt(comparator_2_gt[2]));
  // Probe on comparator_1_gt
  // Probe on comparator_2_gt
  Multiplexer #(.select(2), .width(3)) multiplexer_1 (
    .in0(comparator_1_gt), .in1(comparator_2_gt), .out(multiplexer_1_out), .sel(ControlSignal));  // open: in2, in3
  Multiplexer #(.select(3), .width(2)) multiplexer_2 (
    .in1(2'b01), .in2(2'b00), .in4(2'b11), .out(multiplexer_2_out), .sel(multiplexer_1_out));  // open: in0, in3, in5, in6, in7
  assign SignOutput = {{14{multiplexer_2_out[1]}}, multiplexer_2_out};  // Bit_Extender bit_extender_3

  // Notes on the sheet:
  //   Signed Comparison
  //   Unsigned Comparison
  //   This outputs 1, 0, or -1
endmodule

module lc4_alu_arithmetic (
  input  [15:0] Rs,
  input  [2:0] ArithCTL,
  input  [15:0] Rt,
  input  [1:0] ArithMuxCTL,
  input  [15:0] Instruction,
  output [15:0] ArithmeticOut
);

  wire [15:0] adder_1_out, bit_extender_1_out, bit_extender_2_out, divider_1_out, multiplexer_1_out,
       multiplier_1_out, subtractor_1_out;

  assign bit_extender_1_out = {{11{Instruction[4]}}, Instruction[4:0]};  // Bit_Extender bit_extender_1
  assign bit_extender_2_out = {{10{Instruction[5]}}, Instruction[5:0]};  // Bit_Extender bit_extender_2
  Multiplexer #(.select(2), .width(16)) multiplexer_1 (
    .in0(Rt), .in1(bit_extender_1_out), .in2(bit_extender_2_out), .out(multiplexer_1_out), .sel(ArithMuxCTL));  // open: in3
  Adder #(.width(16)) adder_1 (.a(Rs), .b(multiplexer_1_out), .out(adder_1_out));  // open: cin, cout
  Multiplier #(.width(16)) multiplier_1 (.a(Rs), .b(multiplexer_1_out), .out(multiplier_1_out));  // open: cin, cout
  Subtractor #(.width(16)) subtractor_1 (.a(Rs), .b(multiplexer_1_out), .out(subtractor_1_out));  // open: bin, bout
  Divider #(.width(16)) divider_1 (.a(Rs), .b(multiplexer_1_out), .out(divider_1_out));  // open: upper, rem
  Multiplexer #(.select(3), .width(16)) multiplexer_2 (
    .in0(adder_1_out), .in1(multiplier_1_out), .in2(subtractor_1_out), .in3(divider_1_out),
    .out(ArithmeticOut), .sel(ArithCTL));  // open: in4, in5, in6, in7

  // Notes on the sheet:
  //   This chooses Rt, or SEXT 4:0 or SEXT 5:0
endmodule

module lc4_alu_constant (
  input  ControlSignal,
  input  [15:0] Instruction,
  input  [15:0] Rs,
  output [15:0] ConstOut
);

  wire [15:0] and_1_out, bit_extender_1_out, bit_extender_2_out, or_1_out, shifter_1_out;

  assign bit_extender_1_out = {{7{Instruction[8]}}, Instruction[8:0]};  // Bit_Extender bit_extender_1
  assign bit_extender_2_out = {{8{Instruction[7]}}, Instruction[7:0]};  // Bit_Extender bit_extender_2
  assign and_1_out = Rs & 16'hff;  // AND_Gate and_1, 16 bits wide
  Shifter #(.width(16)) shifter_1 (.in(bit_extender_2_out), .\dist (4'b1000), .out(shifter_1_out));
  assign or_1_out = shifter_1_out | and_1_out;  // OR_Gate or_1, 16 bits wide
  Multiplexer #(.width(16)) multiplexer_1 (
    .in0(bit_extender_1_out), .in1(or_1_out), .out(ConstOut), .sel(ControlSignal));

  // Notes on the sheet:
  //   (Rs AND x00FF) OR (UIMM8 <<8)
endmodule

module lc4_alu_shift (
  input  [1:0] ControlSignal,
  input  [15:0] Rs,
  input  [15:0] Instruction,
  output [15:0] ShiftOutput
);

  wire [15:0] shifter_1_out, shifter_2_out, shifter_3_out;

  // Probe on Instruction[3:0]
  Shifter #(.width(16)) shifter_1 (.in(Rs), .\dist (Instruction[3:0]), .out(shifter_1_out));
  Shifter #(.shift("ar"), .width(16)) shifter_2 (.in(Rs), .\dist (Instruction[3:0]), .out(shifter_2_out));
  Shifter #(.shift("lr"), .width(16)) shifter_3 (.in(Rs), .\dist (Instruction[3:0]), .out(shifter_3_out));
  Multiplexer #(.select(2), .width(16)) multiplexer_1 (
    .in0(shifter_1_out), .in1(shifter_2_out), .in2(shifter_3_out), .out(ShiftOutput), .sel(ControlSignal));  // open: in3

  // Notes on the sheet:
  //   Shift Left Logical
  //   Shift Right Arithmetic
  //   Shift Right Logical
endmodule

module lc4_alu_logic (
  input  LogicMuxCTL,
  input  [1:0] LogicCTL,
  input  [15:0] Rs,
  input  [15:0] Rt,
  input  [15:0] Instruction,
  output [15:0] LogicOutput
);

  wire [15:0] and_1_out, bit_extender_1_out, multiplexer_1_out, not_1_out, or_1_out, xor_1_out;

  assign bit_extender_1_out = {{11{Instruction[4]}}, Instruction[4:0]};  // Bit_Extender bit_extender_1
  Multiplexer #(.width(16)) multiplexer_1 (
    .in0(Rt), .in1(bit_extender_1_out), .out(multiplexer_1_out), .sel(LogicMuxCTL));
  assign not_1_out = ~Rs;  // NOT_Gate not_1, 16 bits wide
  assign and_1_out = multiplexer_1_out & Rs;  // AND_Gate and_1, 16 bits wide
  assign or_1_out = multiplexer_1_out | Rs;  // OR_Gate or_1, 16 bits wide
  assign xor_1_out = multiplexer_1_out ^ Rs;  // XOR_Gate xor_1, 16 bits wide
  Multiplexer #(.select(2), .width(16)) multiplexer_2 (
    .in0(and_1_out), .in1(not_1_out), .in2(or_1_out), .in3(xor_1_out), .out(LogicOutput), .sel(LogicCTL));
endmodule

module lc4_alu (
  input  [2:0] ALUMuxCTL,
  input  [1:0] ArithMuxCTL,
  input  [2:0] ArithCTL,
  input  [15:0] Rs,
  input  LogicMuxCTL,
  input  [15:0] Rt,
  input  [1:0] LogicCTL,
  input  [15:0] Instruction,
  input  [1:0] ShiftCTL,
  input  ConstCTL,
  input  [1:0] CmpCTL,
  output [15:0] ALUOutput
);

  wire [15:0] lc4_alu_arithmetic_1_arithmeticout, lc4_alu_comparator_1_signoutput,
       lc4_alu_constant_1_constout, lc4_alu_logic_1_logicoutput, lc4_alu_shift_1_shiftoutput;

  lc4_alu_constant lc4_alu_constant_1 (
    .ControlSignal(ConstCTL), .Instruction(Instruction), .Rs(Rs), .ConstOut(lc4_alu_constant_1_constout));
  lc4_alu_logic lc4_alu_logic_1 (
    .LogicMuxCTL(LogicMuxCTL), .LogicCTL(LogicCTL), .Rs(Rs), .Rt(Rt), .Instruction(Instruction),
    .LogicOutput(lc4_alu_logic_1_logicoutput));
  lc4_alu_shift lc4_alu_shift_1 (
    .ControlSignal(ShiftCTL), .Rs(Rs), .Instruction(Instruction), .ShiftOutput(lc4_alu_shift_1_shiftoutput));
  lc4_alu_arithmetic lc4_alu_arithmetic_1 (
    .Rs(Rs), .ArithCTL(ArithCTL), .Rt(Rt), .ArithMuxCTL(ArithMuxCTL), .Instruction(Instruction),
    .ArithmeticOut(lc4_alu_arithmetic_1_arithmeticout));
  lc4_alu_comparator lc4_alu_comparator_1 (
    .ControlSignal(CmpCTL), .Rs(Rs), .Rt(Rt), .Instruction(Instruction),
    .SignOutput(lc4_alu_comparator_1_signoutput));
  Multiplexer #(.select(3), .width(16)) multiplexer_1 (
    .in0(lc4_alu_arithmetic_1_arithmeticout), .in1(lc4_alu_logic_1_logicoutput),
    .in2(lc4_alu_shift_1_shiftoutput), .in3(lc4_alu_constant_1_constout),
    .in4(lc4_alu_comparator_1_signoutput), .out(ALUOutput), .sel(ALUMuxCTL));  // open: in5, in6, in7
endmodule

module lc4_decoder (
  input  [15:0] Instruction,
  output DataWE,
  output NZPWE,
  output [2:0] ALUMuxCTL,
  output [1:0] CmpCTL,
  output ConstCTL,
  output [1:0] ShiftCTL,
  output LogicMuxCTL,
  output [1:0] LogicCTL,
  output [1:0] ArithMuxCTL,
  output [2:0] ArithCTL,
  output [1:0] regInputMuxCTL,
  output regFileWE,
  output rdMuxCTL,
  output rtMuxCTL,
  output [1:0] rsMuxCTL,
  output [2:0] PCMuxCTL
);

  wire [2:0] multiplexer_1_out;
  wire [3:0] bit_extender_1_out, bit_extender_2_out, bit_extender_3_out, bit_extender_4_out,
       bit_extender_5_out, multiplexer_2_out;
  wire [6:0] adder_1_out, bit_extender_6_out, bit_extender_7_out, multiplier_1_out;

  assign bit_extender_1_out = {{1{1'b0}}, Instruction[11:9]};  // Bit_Extender bit_extender_1
  assign bit_extender_2_out = {{2{1'b0}}, Instruction[8:7]};  // Bit_Extender bit_extender_2
  assign bit_extender_3_out = {{3{1'b0}}, Instruction[11]};  // Bit_Extender bit_extender_3
  assign bit_extender_4_out = {{2{1'b0}}, Instruction[5:4]};  // Bit_Extender bit_extender_4
  Multiplexer #(.width(3)) multiplexer_1 (
    .in0(Instruction[5:3]), .in1(3'b100), .out(multiplexer_1_out), .sel(Instruction[5]));
  assign bit_extender_5_out = {{1{1'b0}}, multiplexer_1_out};  // Bit_Extender bit_extender_5
  assign bit_extender_6_out = {{3{1'b0}}, Instruction[15:12]};  // Bit_Extender bit_extender_6
  Multiplexer #(.select(4), .width(4)) multiplexer_2 (
    .in0(bit_extender_1_out), .in1(bit_extender_5_out), .in2(bit_extender_2_out), .in4(bit_extender_3_out),
    .in5(bit_extender_5_out), .in6(4'b0000), .in7(4'b0000), .in8(4'b0000), .in9(4'b0000),
    .in10(bit_extender_4_out), .in12(bit_extender_3_out), .in13(4'b0000), .in15(4'b0000),
    .out(multiplexer_2_out), .sel(Instruction[15:12]));  // open: in3, in11, in14
  Multiplier #(.width(7)) multiplier_1 (
    .a(bit_extender_6_out), .b(7'b0001000), .out(multiplier_1_out));  // open: cin, cout
  assign bit_extender_7_out = {{3{1'b0}}, multiplexer_2_out};  // Bit_Extender bit_extender_7
  // Probe on bit_extender_7_out
  // Probe on multiplier_1_out
  // Probe on adder_1_out
  Adder #(.width(7)) adder_1 (.a(bit_extender_7_out), .b(multiplier_1_out), .out(adder_1_out));  // open: cin, cout
  ROM #(.addrWidth(7), .dataWidth(28)) rom_1 (
    .addr(adder_1_out),
    .data({PCMuxCTL, rsMuxCTL, rtMuxCTL, rdMuxCTL, regFileWE, regInputMuxCTL, ArithCTL, ArithMuxCTL, LogicCTL, LogicMuxCTL, ShiftCTL, ConstCTL, CmpCTL, ALUMuxCTL, NZPWE, DataWE}));

  // Notes on the sheet:
  //   NOP or BR subopcode
  //   CMP subopcode
  //   JSR or JSR subopcode
  //   Shift subopcode
  //   Arithmetic or Logic subopcode
  //   Opcode Line
  //   No subopcode
  //   contents of rom_1 (hex, n*v repeats v):
  //   2000000 7*0 2100002 2108002 2110002 2118002 2102002 0 0 0 3000012 3000032 3000052 3000072 12*0
  //   6380002 a380002 6*0 2100006 2100806 2101006 2101806 2100406 0 0 0 2144002 7*0 2404001 15*0 210000e
  //   23*0 6000000 4000000 6*0 310008e
  //   Index = OpCode x 8 + Offset
  //   Control signal lookup table
endmodule

module lc4_branch_unit_splitter (
  input  [15:0] Instruction,
  output [10:0] I_10_0,
  output [8:0] I_8_0,
  output [2:0] I_11_9,
  output [7:0] I_7_0
);


  assign I_7_0 = Instruction[7:0];
  assign I_8_0 = Instruction[8:0];
  assign I_10_0 = Instruction[10:0];
  assign I_11_9 = Instruction[11:9];
endmodule

module lc4_branch_unit_comb (
  input  [15:0] Instruction,
  input  [2:0] NZPInput,
  input  [2:0] PCMuxCTL,
  input  [15:0] Rs,
  input  [15:0] PCInput,
  output [15:0] PCOutput
);

  wire lc4_tester_1_result;
  wire [2:0] lc4_branch_unit_splitter_1_i_11_9;
  wire [7:0] lc4_branch_unit_splitter_1_i_7_0;
  wire [8:0] lc4_branch_unit_splitter_1_i_8_0;
  wire [10:0] lc4_branch_unit_splitter_1_i_10_0, shifter_1_out;
  wire [15:0] adder_1_out, adder_2_out, and_1_out, bit_extender_1_out, bit_extender_2_out,
       bit_extender_3_out, bit_extender_4_out, multiplexer_2_out, or_1_out, or_2_out;

  Multiplexer #(.select(3), .width(16)) multiplexer_1 (
    .in0(multiplexer_2_out), .in1(PCInput), .in2(adder_2_out), .in3(Rs), .in4(or_2_out), .in5(or_1_out),
    .out(PCOutput), .sel(PCMuxCTL));  // open: in6, in7
  lc4_branch_unit_splitter lc4_branch_unit_splitter_1 (
    .Instruction(Instruction), .I_10_0(lc4_branch_unit_splitter_1_i_10_0),
    .I_8_0(lc4_branch_unit_splitter_1_i_8_0), .I_11_9(lc4_branch_unit_splitter_1_i_11_9),
    .I_7_0(lc4_branch_unit_splitter_1_i_7_0));
  assign or_1_out = bit_extender_4_out | and_1_out;  // OR_Gate or_1, 16 bits wide
  assign and_1_out = 16'h8000 & PCInput;  // AND_Gate and_1, 16 bits wide
  lc4_tester lc4_tester_1 (
    .NZPRegister(NZPInput), .Instruction_11_9(lc4_branch_unit_splitter_1_i_11_9), .Result(lc4_tester_1_result));
  Multiplexer #(.width(16)) multiplexer_2 (
    .in0(PCInput), .in1(adder_1_out), .out(multiplexer_2_out), .sel(lc4_tester_1_result));
  assign bit_extender_1_out = {{7{lc4_branch_unit_splitter_1_i_8_0[8]}}, lc4_branch_unit_splitter_1_i_8_0};  // Bit_Extender bit_extender_1
  assign bit_extender_2_out = {{5{lc4_branch_unit_splitter_1_i_10_0[10]}}, lc4_branch_unit_splitter_1_i_10_0};  // Bit_Extender bit_extender_2
  Adder #(.width(16)) adder_1 (.a(bit_extender_1_out), .b(PCInput), .out(adder_1_out));  // open: cin, cout
  Adder #(.width(16)) adder_2 (.a(bit_extender_2_out), .b(PCInput), .out(adder_2_out));  // open: cin, cout
  assign or_2_out = bit_extender_3_out | 16'h8000;  // OR_Gate or_2, 16 bits wide
  assign bit_extender_3_out = {{8{1'b0}}, lc4_branch_unit_splitter_1_i_7_0};  // Bit_Extender bit_extender_3
  assign bit_extender_4_out = {{5{1'b0}}, shifter_1_out};  // Bit_Extender bit_extender_4
  Shifter #(.width(11)) shifter_1 (.in(lc4_branch_unit_splitter_1_i_10_0), .\dist (4'b0100), .out(shifter_1_out));
  // Probe on bit_extender_4_out

  // Notes on the sheet:
  //   Represents PC+1
  //   PCInput + SEXT(I[10:0])
  //   0x8000 OR UIMM8
  //   Shift IMM11 To the Left by 4 and extend with zero to 16 bits
endmodule

module lc4_nzp (
  input  [15:0] RegFileInput,
  output [2:0] NZPOut
);

  wire not_2_out, or_1_out;

  or or_1 (or_1_out, RegFileInput[15], RegFileInput[14], RegFileInput[13], RegFileInput[12], RegFileInput[11], RegFileInput[10], RegFileInput[9], RegFileInput[8], RegFileInput[7], RegFileInput[6], RegFileInput[5], RegFileInput[4], RegFileInput[3], RegFileInput[2], RegFileInput[1], RegFileInput[0]);
  not not_1 (NZPOut[1], or_1_out);
  not not_2 (not_2_out, RegFileInput[15]);
  and and_1 (NZPOut[0], or_1_out, not_2_out);

  assign NZPOut[2] = RegFileInput[15];

  // Notes on the sheet:
  //   Tried to orient input output lines so that they show up in the right place on the black box
endmodule

module lc4_tester (
  input  [2:0] NZPRegister,
  input  [2:0] Instruction_11_9,
  output Result
);

  wire and_1_out, and_2_out, and_3_out;

  and and_1 (and_1_out, NZPRegister[2], Instruction_11_9[2]);
  and and_2 (and_2_out, NZPRegister[1], Instruction_11_9[1]);
  or or_1 (Result, and_1_out, and_2_out, and_3_out);
  and and_3 (and_3_out, NZPRegister[0], Instruction_11_9[0]);
endmodule

module lc4_first_iteration (
  input  CLOCK
);

  wire decoder_variant_1_output1, decoder_variant_1_output2, decoder_variant_1_output3,
       decoder_variant_1_output4, decoder_variant_1_output5, decoder_variant_1_output6,
       decoder_variant_1_output7, decoder_variant_1_output8, lc4_decoder_1_constctl,
       lc4_decoder_1_logicmuxctl, lc4_decoder_1_nzpwe, lc4_decoder_1_rdmuxctl, lc4_decoder_1_regfilewe,
       lc4_decoder_1_rtmuxctl;
  wire [1:0] lc4_decoder_1_arithmuxctl, lc4_decoder_1_cmpctl, lc4_decoder_1_logicctl,
       lc4_decoder_1_reginputmuxctl, lc4_decoder_1_rsmuxctl, lc4_decoder_1_shiftctl;
  wire [2:0] lc4_decoder_1_alumuxctl, lc4_decoder_1_arithctl, lc4_decoder_1_pcmuxctl, multiplexer_1_out,
       multiplexer_2_out, multiplexer_3_out, NZPRegister_q, NZPTester_nzpout, PMemory_data, PMemory_data_3,
       PMemory_data_4;
  wire [15:0] adder_1_out, lc4_alu_1_aluoutput, lc4_branch_unit_comb_1_pcoutput, multiplexer_4_out,
       mux_two_in_out_1_output1, mux_two_in_out_1_output2, PC_q, register_1_q, register_2_q, register_3_q,
       register_4_q, register_5_q, register_6_q, register_7_q, register_8_q;
  wire [15:3] PMemory_data_2;

  Register #(.width(16)) PC (.D(lc4_branch_unit_comb_1_pcoutput), .clk(CLOCK), .Q(PC_q));  // open: en, clr
  ROM #(.addrWidth(16), .dataWidth(16)) PMemory (
    .addr(PC_q),
    .data({PMemory_data_2[15:12], PMemory_data_4, PMemory_data_3, PMemory_data_2[5:3], PMemory_data}));
  Adder #(.width(16)) adder_1 (.a(PC_q), .b(16'h1), .out(adder_1_out));  // open: cin, cout
  // Probe on {PMemory_data_2[15:12], PMemory_data_4, PMemory_data_3, PMemory_data_2[5:3], PMemory_data}
  lc4_branch_unit_comb lc4_branch_unit_comb_1 (
    .Instruction({PMemory_data_2[15:12], PMemory_data_4, PMemory_data_3, PMemory_data_2[5:3], PMemory_data}),
    .NZPInput(NZPRegister_q), .PCMuxCTL(lc4_decoder_1_pcmuxctl), .Rs(mux_two_in_out_1_output1),
    .PCInput(adder_1_out), .PCOutput(lc4_branch_unit_comb_1_pcoutput));
  lc4_decoder lc4_decoder_1 (
    .Instruction({PMemory_data_2[15:12], PMemory_data_4, PMemory_data_3, PMemory_data_2[5:3], PMemory_data}),
    .NZPWE(lc4_decoder_1_nzpwe), .ALUMuxCTL(lc4_decoder_1_alumuxctl), .CmpCTL(lc4_decoder_1_cmpctl),
    .ConstCTL(lc4_decoder_1_constctl), .ShiftCTL(lc4_decoder_1_shiftctl),
    .LogicMuxCTL(lc4_decoder_1_logicmuxctl), .LogicCTL(lc4_decoder_1_logicctl),
    .ArithMuxCTL(lc4_decoder_1_arithmuxctl), .ArithCTL(lc4_decoder_1_arithctl),
    .regInputMuxCTL(lc4_decoder_1_reginputmuxctl), .regFileWE(lc4_decoder_1_regfilewe),
    .rdMuxCTL(lc4_decoder_1_rdmuxctl), .rtMuxCTL(lc4_decoder_1_rtmuxctl), .rsMuxCTL(lc4_decoder_1_rsmuxctl),
    .PCMuxCTL(lc4_decoder_1_pcmuxctl));  // open: DataWE
  // Probe on lc4_branch_unit_comb_1_pcoutput
  Register #(.width(3)) NZPRegister (
    .D(NZPTester_nzpout), .en(lc4_decoder_1_nzpwe), .clk(CLOCK), .Q(NZPRegister_q));  // open: clr
  Multiplexer #(.width(3)) multiplexer_1 (
    .in0(PMemory_data_4), .in1(3'b111), .out(multiplexer_1_out), .sel(lc4_decoder_1_rdmuxctl));
  lc4_nzp NZPTester (.NZPOut(NZPTester_nzpout), .RegFileInput(multiplexer_4_out));
  Multiplexer #(.select(2), .width(3)) multiplexer_2 (
    .in0(PMemory_data_3), .in1(3'b111), .in2(PMemory_data_4), .out(multiplexer_2_out),
    .sel(lc4_decoder_1_rsmuxctl));  // open: in3
  Multiplexer #(.width(3)) multiplexer_3 (
    .in0(PMemory_data), .in1(PMemory_data_4), .out(multiplexer_3_out), .sel(lc4_decoder_1_rtmuxctl));
  decoder_variant decoder_variant_1 (
    .WE(lc4_decoder_1_regfilewe), .in_2(multiplexer_1_out), .Output1(decoder_variant_1_output1),
    .Output2(decoder_variant_1_output2), .Output3(decoder_variant_1_output3),
    .Output4(decoder_variant_1_output4), .Output5(decoder_variant_1_output5),
    .Output6(decoder_variant_1_output6), .Output7(decoder_variant_1_output7),
    .Output8(decoder_variant_1_output8));
  // Probe on multiplexer_4_out
  Register #(.width(16)) register_1 (
    .D(multiplexer_4_out), .en(decoder_variant_1_output1), .clk(CLOCK), .Q(register_1_q));  // open: clr
  Register #(.width(16)) register_2 (
    .D(multiplexer_4_out), .en(decoder_variant_1_output2), .clk(CLOCK), .Q(register_2_q));  // open: clr
  Register #(.width(16)) register_3 (
    .D(multiplexer_4_out), .en(decoder_variant_1_output3), .clk(CLOCK), .Q(register_3_q));  // open: clr
  Register #(.width(16)) register_4 (
    .D(multiplexer_4_out), .en(decoder_variant_1_output4), .clk(CLOCK), .Q(register_4_q));  // open: clr
  Register #(.width(16)) register_5 (
    .D(multiplexer_4_out), .en(decoder_variant_1_output5), .clk(CLOCK), .Q(register_5_q));  // open: clr
  Register #(.width(16)) register_6 (
    .D(multiplexer_4_out), .en(decoder_variant_1_output6), .clk(CLOCK), .Q(register_6_q));  // open: clr
  Register #(.width(16)) register_7 (
    .D(multiplexer_4_out), .en(decoder_variant_1_output7), .clk(CLOCK), .Q(register_7_q));  // open: clr
  Register #(.width(16)) register_8 (
    .D(multiplexer_4_out), .en(decoder_variant_1_output8), .clk(CLOCK), .Q(register_8_q));  // open: clr
  mux_two_in_out mux_two_in_out_1 (
    .Input1(register_1_q), .Input2(register_2_q), .Input3(register_3_q), .Input4(register_4_q),
    .Input5(register_5_q), .Input6(register_6_q), .Input7(register_7_q), .Input8(register_8_q),
    .Select1(multiplexer_2_out), .Select2(multiplexer_3_out), .Output1(mux_two_in_out_1_output1),
    .Output2(mux_two_in_out_1_output2));
  // Probe on mux_two_in_out_1_output1
  // Probe on mux_two_in_out_1_output2
  lc4_alu lc4_alu_1 (
    .ALUMuxCTL(lc4_decoder_1_alumuxctl), .ArithMuxCTL(lc4_decoder_1_arithmuxctl),
    .ArithCTL(lc4_decoder_1_arithctl), .Rs(mux_two_in_out_1_output1),
    .LogicMuxCTL(lc4_decoder_1_logicmuxctl), .Rt(mux_two_in_out_1_output2),
    .LogicCTL(lc4_decoder_1_logicctl),
    .Instruction({PMemory_data_2[15:12], PMemory_data_4, PMemory_data_3, PMemory_data_2[5:3], PMemory_data}),
    .ShiftCTL(lc4_decoder_1_shiftctl), .ConstCTL(lc4_decoder_1_constctl), .CmpCTL(lc4_decoder_1_cmpctl),
    .ALUOutput(lc4_alu_1_aluoutput));
  Multiplexer #(.select(2), .width(16)) multiplexer_4 (
    .in0(lc4_alu_1_aluoutput), .in3(adder_1_out), .out(multiplexer_4_out), .sel(lc4_decoder_1_reginputmuxctl));  // open: in1, in2

  // Notes on the sheet:
  //   contents of PMemory (hex, n*v repeats v):
  //   9000 9201 9403 9607 980a 9a0f 9c10 9eff d1ff
  //   Rd MUX
  //   Rs MUX
  //   Rt MUX
  //   Register File Input MUX
endmodule

module lc4 (
);

  wire CLK, ConstCTL, DataWE, decoder_1_out0, decoder_1_out1, decoder_1_out2, decoder_1_out3, decoder_1_out4,
       decoder_1_out5, decoder_1_out6, decoder_1_out7, lc4_decoder_1_rdmuxctl, lc4_decoder_1_regfilewe,
       lc4_decoder_1_rtmuxctl, LogicMuxCTL, NZPWE;
  wire [1:0] ArithMuxCTL, CmpCTL, lc4_decoder_1_rsmuxctl, LogicCTL, regInputMuxCTL, ShiftCTL;
  wire [2:0] ALUMuxCTL, ArithCTL, multiplexer_1_out, multiplexer_2_out, multiplexer_3_out, NZPRegister,
       NZPTester_nzpout, PCMuxCTL;
  wire [15:0] ALUOutput, BranchUnitOutput, DataMemory_dout, INSTRUCTION, PC_q, PCPlusOne, regInput,
       register_1_q, register_2_q, register_3_q, register_4_q, register_5_q, register_6_q, register_7_q,
       register_8_q, Rs, Rt;

  Clock clock_1 (.out(CLK));
  // Probe on NZPRegister
  // Probe on ALUOutput
  // Probe on INSTRUCTION
  // Probe on regInput
  Register #(.width(16)) PC (.D(BranchUnitOutput), .clk(CLK), .Q(PC_q));  // open: en, clr
  ROM #(.addrWidth(16), .dataWidth(16)) PMemory (.addr(PC_q), .data(INSTRUCTION));
  Adder #(.width(16)) adder_1 (.a(PC_q), .b(16'h1), .out(PCPlusOne));  // open: cin, cout
  lc4_branch_unit_comb lc4_branch_unit_comb_1 (
    .Instruction(INSTRUCTION), .NZPInput(NZPRegister), .PCMuxCTL(PCMuxCTL), .Rs(Rs), .PCInput(PCPlusOne),
    .PCOutput(BranchUnitOutput));
  lc4_decoder lc4_decoder_1 (
    .Instruction(INSTRUCTION), .DataWE(DataWE), .NZPWE(NZPWE), .ALUMuxCTL(ALUMuxCTL), .CmpCTL(CmpCTL),
    .ConstCTL(ConstCTL), .ShiftCTL(ShiftCTL), .LogicMuxCTL(LogicMuxCTL), .LogicCTL(LogicCTL),
    .ArithMuxCTL(ArithMuxCTL), .ArithCTL(ArithCTL), .regInputMuxCTL(regInputMuxCTL),
    .regFileWE(lc4_decoder_1_regfilewe), .rdMuxCTL(lc4_decoder_1_rdmuxctl),
    .rtMuxCTL(lc4_decoder_1_rtmuxctl), .rsMuxCTL(lc4_decoder_1_rsmuxctl), .PCMuxCTL(PCMuxCTL));
  Register #(.width(3)) u_NZPRegister (.D(NZPTester_nzpout), .en(NZPWE), .clk(CLK), .Q(NZPRegister));  // open: clr
  Multiplexer #(.width(3)) multiplexer_1 (
    .in0(INSTRUCTION[11:9]), .in1(3'b111), .out(multiplexer_1_out), .sel(lc4_decoder_1_rdmuxctl));
  lc4_nzp NZPTester (.NZPOut(NZPTester_nzpout), .RegFileInput(regInput));
  Multiplexer #(.select(2), .width(3)) multiplexer_2 (
    .in0(INSTRUCTION[8:6]), .in1(3'b111), .in2(INSTRUCTION[11:9]), .out(multiplexer_2_out),
    .sel(lc4_decoder_1_rsmuxctl));  // open: in3
  Multiplexer #(.width(3)) multiplexer_3 (
    .in0(INSTRUCTION[2:0]), .in1(INSTRUCTION[11:9]), .out(multiplexer_3_out), .sel(lc4_decoder_1_rtmuxctl));
  Decoder #(.select(3)) decoder_1 (
    .out0(decoder_1_out0), .out1(decoder_1_out1), .out2(decoder_1_out2), .out3(decoder_1_out3),
    .out4(decoder_1_out4), .out5(decoder_1_out5), .out6(decoder_1_out6), .out7(decoder_1_out7),
    .sel(multiplexer_1_out), .en(lc4_decoder_1_regfilewe));
  Register #(.width(16)) register_1 (.D(regInput), .en(decoder_1_out0), .clk(CLK), .Q(register_1_q));  // open: clr
  Register #(.width(16)) register_2 (.D(regInput), .en(decoder_1_out1), .clk(CLK), .Q(register_2_q));  // open: clr
  Register #(.width(16)) register_3 (.D(regInput), .en(decoder_1_out2), .clk(CLK), .Q(register_3_q));  // open: clr
  Register #(.width(16)) register_4 (.D(regInput), .en(decoder_1_out3), .clk(CLK), .Q(register_4_q));  // open: clr
  Register #(.width(16)) register_5 (.D(regInput), .en(decoder_1_out4), .clk(CLK), .Q(register_5_q));  // open: clr
  Register #(.width(16)) register_6 (.D(regInput), .en(decoder_1_out5), .clk(CLK), .Q(register_6_q));  // open: clr
  Register #(.width(16)) register_7 (.D(regInput), .en(decoder_1_out6), .clk(CLK), .Q(register_7_q));  // open: clr
  Register #(.width(16)) register_8 (.D(regInput), .en(decoder_1_out7), .clk(CLK), .Q(register_8_q));  // open: clr
  mux_two_in_out mux_two_in_out_1 (
    .Input1(register_1_q), .Input2(register_2_q), .Input3(register_3_q), .Input4(register_4_q),
    .Input5(register_5_q), .Input6(register_6_q), .Input7(register_7_q), .Input8(register_8_q),
    .Select1(multiplexer_2_out), .Select2(multiplexer_3_out), .Output1(Rs), .Output2(Rt));
  lc4_alu lc4_alu_1 (
    .ALUMuxCTL(ALUMuxCTL), .ArithMuxCTL(ArithMuxCTL), .ArithCTL(ArithCTL), .Rs(Rs),
    .LogicMuxCTL(LogicMuxCTL), .Rt(Rt), .LogicCTL(LogicCTL), .Instruction(INSTRUCTION), .ShiftCTL(ShiftCTL),
    .ConstCTL(ConstCTL), .CmpCTL(CmpCTL), .ALUOutput(ALUOutput));
  RAM #(.addrWidth(16), .dataWidth(16)) DataMemory (
    .addr(ALUOutput), .we(DataWE), .clk(CLK), .din(Rt), .dout(DataMemory_dout));  // open: oe
  Multiplexer #(.select(2), .width(16)) multiplexer_4 (
    .in0(ALUOutput), .in1(DataMemory_dout), .in2(PCPlusOne), .out(regInput), .sel(regInputMuxCTL));  // open: in3

  // Notes on the sheet:
  //   CLOCK
  //   contents of PMemory (hex, n*v repeats v):
  //   9000 9201 9403 9607 980a 9a0f 9c10 9eff d1ff
  //   Rd MUX
  //   Rs MUX
  //   Rt MUX
  //   Register File Input MUX
endmodule
