// Logisim project simple_cpu.circ as structural Verilog: 10 circuits, main circuit simple_cpu
module mux_two_in_out (
  input  [15:0] Input1,
  input  [15:0] Input2,
  input  [15:0] Input3,
  input  [15:0] Input4,
  input  [15:0] Input5,
  input  [15:0] Input6,
  input  [15:0] Input7,
  input  [15:0] Input8,
  input  [2:0] Select1,
  input  [2:0] Select2,
  output [15:0] Output1,
  output [15:0] Output2
);

  Multiplexer #(.select(3), .width(16)) multiplexer_1 (
    .in0(Input1), .in1(Input2), .in2(Input3), .in3(Input4), .in4(Input5), .in5(Input6), .in6(Input7),
    .in7(Input8), .out(Output1), .sel(Select1));
  Multiplexer #(.select(3), .width(16)) multiplexer_2 (
    .in0(Input1), .in1(Input2), .in2(Input3), .in3(Input4), .in4(Input5), .in5(Input6), .in6(Input7),
    .in7(Input8), .out(Output2), .sel(Select2));

  // Notes on the sheet:
  //   A MUX variation which has two select lines and two output lines.
endmodule

module mux_two_in_out_4 (
  input  [3:0] Input1,
  input  [3:0] Input2,
  input  [3:0] Input3,
  input  [3:0] Input4,
  input  [3:0] Input5,
  input  [3:0] Input6,
  input  [3:0] Input7,
  input  [3:0] Input8,
  input  [2:0] Select1,
  input  [2:0] Select2,
  output [3:0] Output1,
  output [3:0] Output2
);

  Multiplexer #(.select(3), .width(4)) multiplexer_1 (
    .in0(Input1), .in1(Input2), .in2(Input3), .in3(Input4), .in4(Input5), .in5(Input6), .in6(Input7),
    .in7(Input8), .out(Output2), .sel(Select2));
  Multiplexer #(.select(3), .width(4)) multiplexer_2 (
    .in0(Input1), .in1(Input2), .in2(Input3), .in3(Input4), .in4(Input5), .in5(Input6), .in6(Input7),
    .in7(Input8), .out(Output1), .sel(Select1));
endmodule

module simple_memory_register (
  input  Clock,
  input  WE,
  input  [2:0] AddressWrite,
  input  [15:0] DataIn,
  input  [2:0] AddressRead1,
  input  [2:0] AddressRead2,
  output [15:0] DataOut1,
  output [15:0] DataOut2
);

  wire decoder_1_out0, decoder_1_out1, decoder_1_out2, decoder_1_out3, decoder_1_out4, decoder_1_out5,
       decoder_1_out6, decoder_1_out7;
  wire [15:0] register_1_q, register_2_q, register_3_q, register_4_q, register_5_q, register_6_q,
       register_7_q, register_8_q;

  Decoder #(.select(3)) decoder_1 (
    .out0(decoder_1_out0), .out1(decoder_1_out1), .out2(decoder_1_out2), .out3(decoder_1_out3),
    .out4(decoder_1_out4), .out5(decoder_1_out5), .out6(decoder_1_out6), .out7(decoder_1_out7),
    .sel(AddressWrite), .en(WE));
  Register #(.width(16)) register_1 (.D(DataIn), .en(decoder_1_out0), .clk(Clock), .Q(register_1_q));  // open: clr
  Register #(.width(16)) register_2 (.D(DataIn), .en(decoder_1_out1), .clk(Clock), .Q(register_2_q));  // open: clr
  Register #(.width(16)) register_3 (.D(DataIn), .en(decoder_1_out2), .clk(Clock), .Q(register_3_q));  // open: clr
  Register #(.width(16)) register_4 (.D(DataIn), .en(decoder_1_out3), .clk(Clock), .Q(register_4_q));  // open: clr
  Register #(.width(16)) register_5 (.D(DataIn), .en(decoder_1_out4), .clk(Clock), .Q(register_5_q));  // open: clr
  Register #(.width(16)) register_6 (.D(DataIn), .en(decoder_1_out5), .clk(Clock), .Q(register_6_q));  // open: clr
  Register #(.width(16)) register_7 (.D(DataIn), .en(decoder_1_out6), .clk(Clock), .Q(register_7_q));  // open: clr
  Register #(.width(16)) register_8 (.D(DataIn), .en(decoder_1_out7), .clk(Clock), .Q(register_8_q));  // open: clr
  mux_two_in_out mux_two_in_out_1 (
    .Input1(register_1_q), .Input2(register_2_q), .Input3(register_3_q), .Input4(register_4_q),
    .Input5(register_5_q), .Input6(register_6_q), .Input7(register_7_q), .Input8(register_8_q),
    .Select1(AddressRead1), .Select2(AddressRead2), .Output1(DataOut1), .Output2(DataOut2));

  // Notes on the sheet:
  //   8 by 16 Register File
endmodule

module simple_cpu_nzp (
  input  [15:0] DataIn,
  input  [2:0] NZP,
  output Output
);

  wire NegTest_out, not_1_out, not_2_out, or_1_out, PosTest_out, ZeroTest_out;

  or or_1 (or_1_out, DataIn[15], DataIn[14], DataIn[13], DataIn[12], DataIn[11], DataIn[10], DataIn[9], DataIn[8], DataIn[7], DataIn[6], DataIn[5], DataIn[4], DataIn[3], DataIn[2], DataIn[1], DataIn[0]);
  not not_1 (not_1_out, DataIn[15]);
  not not_2 (not_2_out, or_1_out);
  and NegTest (NegTest_out, DataIn[15], NZP[2]);
  and PosTest (PosTest_out, not_1_out, or_1_out, NZP[0]);
  and ZeroTest (ZeroTest_out, not_2_out, NZP[1]);
  or or_2 (Output, ZeroTest_out, NegTest_out, PosTest_out);
endmodule

module simple_cpu_alu (
  input  [15:0] Input1,
  input  [15:0] Input2,
  input  AddOrSub,
  output [15:0] Output
);

  wire [15:0] adder_1_out, subtractor_1_out;

  Adder #(.width(16)) adder_1 (.a(Input2), .b(Input1), .out(adder_1_out));  // open: cin, cout
  Subtractor #(.width(16)) subtractor_1 (.a(Input1), .b(Input2), .out(subtractor_1_out));  // open: bin, bout
  Multiplexer #(.enable("true"), .width(16)) multiplexer_1 (
    .in0(adder_1_out), .in1(subtractor_1_out), .out(Output), .sel(AddOrSub));  // open: en
endmodule

module simple_cpu (
  output [7:0] CLK_Counter_Output,
  output halt,
  output [2:0] PC_Output,
  output [15:0] ALUOutput_Output,
  output [15:0] R0_Output,
  output [15:0] R1_Output,
  output [15:0] R2_Output,
  output [15:0] R3_Output,
  output [15:0] R4_Output
);

  wire ALUOp, CLK, decoder_1_out0, decoder_1_out1, decoder_1_out2, decoder_1_out3, decoder_1_out4,
       decoder_1_out5, decoder_1_out6, decoder_1_out7, TestOutput;
  wire [2:0] adder_2_out, AddrW, multiplexer_1_out;
  wire [7:0] adder_1_out;
  wire [15:0] ControlMemory_data, MUX_output1, MUX_output2, R5, R6, R7;

  Adder adder_1 (.a(CLK_Counter_Output), .b(8'h1), .out(adder_1_out));  // open: cin, cout
  Clock clock_1 (.out(CLK));
  Register CLK_COUNTER (.D(adder_1_out), .clk(CLK), .Q(CLK_Counter_Output));  // open: en, clr
  ROM #(.addrWidth(3), .dataWidth(17)) ControlMemory (
    .addr(PC_Output), .data({ALUOp, ControlMemory_data[15:10], AddrW, ControlMemory_data[6:0]}));
  Comparator comparator_1 (.a(CLK_Counter_Output), .b(8'hf), .eq(halt));  // open: gt, lt
  Register #(.width(3)) PC (.D(multiplexer_1_out), .clk(CLK), .Q(PC_Output));  // open: en, clr
  Adder #(.width(3)) adder_2 (.a(PC_Output), .b(3'b001), .out(adder_2_out));  // open: cin, cout
  Decoder #(.select(3)) decoder_1 (
    .out0(decoder_1_out0), .out1(decoder_1_out1), .out2(decoder_1_out2), .out3(decoder_1_out3),
    .out4(decoder_1_out4), .out5(decoder_1_out5), .out6(decoder_1_out6), .out7(decoder_1_out7), .sel(AddrW),
    .en(ControlMemory_data[6]));
  Register #(.width(16)) register_1 (.D(ALUOutput_Output), .en(decoder_1_out0), .clk(CLK), .Q(R0_Output));  // open: clr
  Register #(.width(16)) register_2 (.D(ALUOutput_Output), .en(decoder_1_out1), .clk(CLK), .Q(R1_Output));  // open: clr
  Register #(.width(16)) register_3 (.D(ALUOutput_Output), .en(decoder_1_out2), .clk(CLK), .Q(R2_Output));  // open: clr
  Register #(.width(16)) register_4 (.D(ALUOutput_Output), .en(decoder_1_out3), .clk(CLK), .Q(R3_Output));  // open: clr
  Register #(.width(16)) register_5 (.D(ALUOutput_Output), .en(decoder_1_out4), .clk(CLK), .Q(R4_Output));  // open: clr
  Register #(.width(16)) register_6 (.D(ALUOutput_Output), .en(decoder_1_out5), .clk(CLK), .Q(R5));  // open: clr
  Register #(.width(16)) register_7 (.D(ALUOutput_Output), .en(decoder_1_out6), .clk(CLK), .Q(R6));  // open: clr
  Register #(.width(16)) register_8 (.D(ALUOutput_Output), .en(decoder_1_out7), .clk(CLK), .Q(R7));  // open: clr
  simple_cpu_nzp simple_cpu_nzp_1 (.DataIn(ALUOutput_Output), .NZP(ControlMemory_data[5:3]), .Output(TestOutput));
  Multiplexer #(.width(3)) multiplexer_1 (
    .in0(adder_2_out), .in1(ControlMemory_data[2:0]), .out(multiplexer_1_out), .sel(TestOutput));
  // Probe on multiplexer_1_out
  mux_two_in_out MUX (
    .Input1(R0_Output), .Input2(R1_Output), .Input3(R2_Output), .Input4(R3_Output), .Input5(R4_Output),
    .Input6(R5), .Input7(R6), .Input8(R7), .Select1(ControlMemory_data[15:13]),
    .Select2(ControlMemory_data[12:10]), .Output1(MUX_output1), .Output2(MUX_output2));
  simple_cpu_alu simple_cpu_alu_1 (
    .Input1(MUX_output1), .Input2(MUX_output2), .AddOrSub(ALUOp), .Output(ALUOutput_Output));

  // Other names for the same wires on the sheet: ALUOutput[15:0] = ALUOutput_Output; PC[2:0] = PC_Output;
  //   R0[15:0] = R0_Output; R1[15:0] = R1_Output; R2[15:0] = R2_Output; R3[15:0] = R3_Output; R4[15:0] = R4_Output

  // Notes on the sheet:
  //   contents of ControlMemory (hex, n*v repeats v):
  //   15023 71c0 8678 3b
  //   CPU Dashboard (Outputs ordered below so that it can be tested via command line)
  //   Select (Address Read) Lines
endmodule

module simple_cpu_test (
  output [7:0] CLK_Counter_Output,
  output halt,
  output [2:0] PC_Output,
  output [15:0] ALUOutput_Output,
  output [15:0] R0_Output,
  output [15:0] R1_Output,
  output [15:0] R2_Output,
  output [15:0] R3_Output,
  output [15:0] R4_Output
);

  wire ALUOp, CLK, decoder_1_out0, decoder_1_out1, decoder_1_out2, decoder_1_out3, decoder_1_out4,
       decoder_1_out5, decoder_1_out6, decoder_1_out7, TestOutput;
  wire [2:0] adder_2_out, AddrW, multiplexer_1_out;
  wire [7:0] adder_1_out;
  wire [15:0] ControlMemory_data, MUX_output1, MUX_output2, undriven, undriven_2, undriven_3, undriven_4,
       undriven_5, undriven_6, undriven_7, undriven_8;

  RAM #(.addrWidth(3), .dataWidth(16)) ram_1 ();  // open: addr, we, oe, clk, din, dout
  Adder adder_1 (.a(CLK_Counter_Output), .b(8'h1), .out(adder_1_out));  // open: cin, cout
  Clock clock_1 (.out(CLK));
  Register CLK_COUNTER (.D(adder_1_out), .clk(CLK), .Q(CLK_Counter_Output));  // open: en, clr
  ROM #(.addrWidth(3), .dataWidth(17)) ControlMemory (
    .addr(PC_Output), .data({ALUOp, ControlMemory_data[15:10], AddrW, ControlMemory_data[6:0]}));
  Comparator comparator_1 (.a(CLK_Counter_Output), .b(8'hf), .eq(halt));  // open: gt, lt
  Register #(.width(3)) PC (.D(multiplexer_1_out), .clk(CLK), .Q(PC_Output));  // open: en, clr
  Adder #(.width(3)) adder_2 (.a(PC_Output), .b(3'b001), .out(adder_2_out));  // open: cin, cout
  Decoder #(.select(3)) decoder_1 (
    .out0(decoder_1_out0), .out1(decoder_1_out1), .out2(decoder_1_out2), .out3(decoder_1_out3),
    .out4(decoder_1_out4), .out5(decoder_1_out5), .out6(decoder_1_out6), .out7(decoder_1_out7), .sel(AddrW),
    .en(ControlMemory_data[6]));
  simple_cpu_nzp simple_cpu_nzp_1 (.DataIn(ALUOutput_Output), .NZP(ControlMemory_data[5:3]), .Output(TestOutput));
  Multiplexer #(.width(3)) multiplexer_1 (
    .in0(adder_2_out), .in1(ControlMemory_data[2:0]), .out(multiplexer_1_out), .sel(TestOutput));
  // Probe on multiplexer_1_out
  mux_two_in_out MUX (
    .Input1(undriven_4), .Input2(undriven_2), .Input3(undriven), .Input4(undriven_3), .Input5(undriven_5),
    .Input6(undriven_6), .Input7(undriven_7), .Input8(undriven_8), .Select1(ControlMemory_data[15:13]),
    .Select2(ControlMemory_data[12:10]), .Output1(MUX_output1), .Output2(MUX_output2));
  simple_cpu_alu simple_cpu_alu_1 (
    .Input1(MUX_output1), .Input2(MUX_output2), .AddOrSub(ALUOp), .Output(ALUOutput_Output));

  // Other names for the same wires on the sheet: ALUOutput[15:0] = ALUOutput_Output; PC[2:0] = PC_Output;
  //   R0[15:0] = R0_Output; R1[15:0] = R1_Output; R2[15:0] = R2_Output; R3[15:0] = R3_Output; R4[15:0] = R4_Output

  // Notes on the sheet:
  //   contents of ControlMemory (hex, n*v repeats v):
  //   15023 71c0 8678 3b
  //   CPU Dashboard (Outputs ordered below so that it can be tested via command line)
  //   Select (Address Read) Lines
endmodule

module simple_cpu_min (
  output [7:0] CLK_Counter_Output,
  output halt,
  output [2:0] PC_Output,
  output [3:0] ALUOutput_Output,
  output [3:0] R0_Output,
  output [3:0] R1_Output,
  output [3:0] R2_Output,
  output [3:0] R3_Output,
  output [3:0] R4_Output
);

  wire ALUOp, CLK, decoder_1_out0, decoder_1_out1, decoder_1_out2, decoder_1_out3, decoder_1_out4,
       decoder_1_out5, decoder_1_out6, decoder_1_out7, TestOutput;
  wire [2:0] adder_2_out, AddrW, multiplexer_1_out;
  wire [3:0] mux_two_in_out_4_1_output1, mux_two_in_out_4_1_output2, R5, R6, R7;
  wire [7:0] adder_1_out;
  wire [15:0] ControlMemory_data;

  Adder adder_1 (.a(CLK_Counter_Output), .b(8'h1), .out(adder_1_out));  // open: cin, cout
  Clock clock_1 (.out(CLK));
  Register CLK_COUNTER (.D(adder_1_out), .clk(CLK), .Q(CLK_Counter_Output));  // open: en, clr
  ROM #(.addrWidth(3), .dataWidth(17)) ControlMemory (
    .addr(PC_Output), .data({ALUOp, ControlMemory_data[15:10], AddrW, ControlMemory_data[6:0]}));
  Comparator comparator_1 (.a(CLK_Counter_Output), .b(8'hf), .eq(halt));  // open: gt, lt
  Register #(.width(3)) PC (.D(multiplexer_1_out), .clk(CLK), .Q(PC_Output));  // open: en, clr
  Adder #(.width(3)) adder_2 (.a(PC_Output), .b(3'b001), .out(adder_2_out));  // open: cin, cout
  Decoder #(.select(3)) decoder_1 (
    .out0(decoder_1_out0), .out1(decoder_1_out1), .out2(decoder_1_out2), .out3(decoder_1_out3),
    .out4(decoder_1_out4), .out5(decoder_1_out5), .out6(decoder_1_out6), .out7(decoder_1_out7), .sel(AddrW),
    .en(ControlMemory_data[6]));
  Register #(.width(4)) register_1 (.D(ALUOutput_Output), .en(decoder_1_out0), .clk(CLK), .Q(R0_Output));  // open: clr
  Register #(.width(4)) register_2 (.D(ALUOutput_Output), .en(decoder_1_out1), .clk(CLK), .Q(R1_Output));  // open: clr
  Register #(.width(4)) register_3 (.D(ALUOutput_Output), .en(decoder_1_out2), .clk(CLK), .Q(R2_Output));  // open: clr
  Register #(.width(4)) register_4 (.D(ALUOutput_Output), .en(decoder_1_out3), .clk(CLK), .Q(R3_Output));  // open: clr
  Register #(.width(4)) register_5 (.D(ALUOutput_Output), .en(decoder_1_out4), .clk(CLK), .Q(R4_Output));  // open: clr
  Register #(.width(4)) register_6 (.D(ALUOutput_Output), .en(decoder_1_out5), .clk(CLK), .Q(R5));  // open: clr
  Register #(.width(4)) register_7 (.D(ALUOutput_Output), .en(decoder_1_out6), .clk(CLK), .Q(R6));  // open: clr
  Register #(.width(4)) register_8 (.D(ALUOutput_Output), .en(decoder_1_out7), .clk(CLK), .Q(R7));  // open: clr
  sample_cpu_nzp_min sample_cpu_nzp_min_1 (
    .DataIn(ALUOutput_Output), .NZP(ControlMemory_data[5:3]), .Output(TestOutput));
  Multiplexer #(.width(3)) multiplexer_1 (
    .in0(adder_2_out), .in1(ControlMemory_data[2:0]), .out(multiplexer_1_out), .sel(TestOutput));
  // Probe on multiplexer_1_out
  mux_two_in_out_4 mux_two_in_out_4_1 (
    .Input1(R0_Output), .Input2(R1_Output), .Input3(R2_Output), .Input4(R3_Output), .Input5(R4_Output),
    .Input6(R5), .Input7(R6), .Input8(R7), .Select1(ControlMemory_data[15:13]),
    .Select2(ControlMemory_data[12:10]), .Output1(mux_two_in_out_4_1_output1),
    .Output2(mux_two_in_out_4_1_output2));
  simple_cpu_alu_min simple_cpu_alu_min_1 (
    .Input1(mux_two_in_out_4_1_output1), .Input2(mux_two_in_out_4_1_output2), .AddOrSub(ALUOp),
    .Output(ALUOutput_Output));

  // Other names for the same wires on the sheet: ALUOutput[3:0] = ALUOutput_Output; PC[2:0] = PC_Output;
  //   R0[3:0] = R0_Output; R1[3:0] = R1_Output; R2[3:0] = R2_Output; R3[3:0] = R3_Output; R4[3:0] = R4_Output

  // Notes on the sheet:
  //   contents of ControlMemory (hex, n*v repeats v):
  //   15023 71c0 8678 3b
  //   CPU Dashboard (Outputs ordered below so that it can be tested via command line)
  //   Select (Address Read) Lines
endmodule

module simple_cpu_alu_min (
  input  [3:0] Input1,
  input  [3:0] Input2,
  input  AddOrSub,
  output [3:0] Output
);

  wire [3:0] adder_1_out, subtractor_1_out;

  Adder #(.width(4)) adder_1 (.a(Input2), .b(Input1), .out(adder_1_out));  // open: cin, cout
  Subtractor #(.width(4)) subtractor_1 (.a(Input1), .b(Input2), .out(subtractor_1_out));  // open: bin, bout
  Multiplexer #(.enable("true"), .width(4)) multiplexer_1 (
    .in0(adder_1_out), .in1(subtractor_1_out), .out(Output), .sel(AddOrSub));  // open: en
endmodule

module sample_cpu_nzp_min (
  input  [3:0] DataIn,
  input  [2:0] NZP,
  output Output
);

  wire NegTest_out, not_1_out, not_2_out, or_1_out, PosTest_out, ZeroTest_out;

  or or_1 (or_1_out, DataIn[3], DataIn[2], DataIn[1], DataIn[0]);
  not not_1 (not_1_out, DataIn[3]);
  not not_2 (not_2_out, or_1_out);
  and NegTest (NegTest_out, DataIn[3], NZP[2]);
  and ZeroTest (ZeroTest_out, not_2_out, NZP[1]);
  and PosTest (PosTest_out, not_1_out, or_1_out, NZP[0]);
  or or_2 (Output, ZeroTest_out, NegTest_out, PosTest_out);
endmodule
